# Fritzing sketch kbd_projekt (saved by Fritzing 0.9.4)
circuit board: 10.1919cm x 7.96588cm

parts:
  ESP32-S2 = ESP32-S2-DevKitM-1 [part_number=ESP32-S2-DevKitM-1]
  MX1 = Cherry MX Keyswitch Simple
  MX2 = Cherry MX Keyswitch Simple
  MX3 = Cherry MX Keyswitch Simple
  MX4 = Cherry MX Keyswitch Simple
  MX5 = Cherry MX Keyswitch Simple
  MX6 = Cherry MX Keyswitch Simple
  MX7 = Cherry MX Keyswitch Simple
  MX8 = Cherry MX Keyswitch Simple
  MX9 = Cherry MX Keyswitch Simple
  MX10 = Cherry MX Keyswitch Simple
  MX11 = Cherry MX Keyswitch Simple
  MX12 = Cherry MX Keyswitch Simple
  μUSB = USB Connectors [package=usb-microb]
  D14 = Diode [package=sma-diode-kit]
  D15 = Diode [package=sma-diode-kit]
  D16 = Diode [package=sma-diode-kit]
  D17 = Diode [package=sma-diode-kit]
  D18 = Diode [package=sma-diode-kit]
  D19 = Diode [package=sma-diode-kit]
  D20 = Diode [package=sma-diode-kit]
  D21 = Diode [package=sma-diode-kit]
  D22 = Diode [package=sma-diode-kit]
  D23 = Diode [package=sma-diode-kit]
  D24 = Diode [package=sma-diode-kit]
  D25 = Diode [package=sma-diode-kit]

nets:
  Data -: ESP32-S2.19, μUSB.D-
  Data +: ESP32-S2.20, μUSB.D+
  Span 1: ESP32-S2.0, MX10.pin_1, MX11.pin_1, MX12.pin_1
  Span 2: ESP32-S2.1, MX7.pin_1, MX8.pin_1, MX9.pin_1
  Span 3: ESP32-S2.2, MX4.pin_1, MX5.pin_1, MX6.pin_1
  Span 4: ESP32-S2.3, MX1.pin_1, MX2.pin_1, MX3.pin_1
  Row 1: ESP32-S2.10, D14.C, D17.C, D20.C, D23.C
  Row 2: ESP32-S2.11, D15.C, D18.C, D21.C, D24.C
  Row 3: ESP32-S2.12, D16.C, D19.C, D22.C, D25.C
  5V: ESP32-S2.5V, μUSB.VBUS
  Gnd: ESP32-S2.G-42, μUSB.GND
  N1: MX1.pin_2, D14.A
  N2: MX2.pin_2, D15.A
  N3: MX3.pin_2, D16.A
  N4: MX4.pin_2, D17.A
  N5: MX5.pin_2, D18.A
  N6: MX6.pin_2, D19.A
  N7: MX7.pin_2, D20.A
  N8: MX8.pin_2, D21.A
  N9: MX9.pin_2, D22.A
  N10: MX10.pin_2, D23.A
  N11: MX11.pin_2, D24.A
  N12: MX12.pin_2, D25.A

notes:
  Pooky'
  test n°1
  13/04/2021
  CyberDeck Keypad, A 12-key programmable keypad made for a CyberDeck project using an ESP32-S2 for Wi-Fi capabilities., 1
  test 1

custom parts:
  ESP32-S2-DevKitM-1: The DOIT Esp32 DevKit v1 is one of the development board created by DOIT to evaluate the ESP-WROOM-32 module. It is based on the ESP32 microcontroller that boasts Wifi, Bluetooth, Ethernet and Low Power support all in a single chip. (vanepp) Feb 2021: converted to ESP32-S2-DevKitM-1. This module is 42pins long (2x21) and 11 pins width.
  Cherry MX Keyswitch Simple: Cherry MX Keyswitch button for keyboards
