# Fritzing sketch kbd_projekt_encoder (saved by Fritzing 0.9.6b)
circuit board: 10.87cm x 8.35cm

parts:
  MX1 = Cherry MX Keyswitch Simple
  MX2 = Cherry MX Keyswitch Simple
  MX3 = Cherry MX Keyswitch Simple
  MX4 = Cherry MX Keyswitch Simple
  MX5 = Cherry MX Keyswitch Simple
  MX6 = Cherry MX Keyswitch Simple
  MX7 = Cherry MX Keyswitch Simple
  MX8 = Cherry MX Keyswitch Simple
  MX9 = Cherry MX Keyswitch Simple
  MX10 = Cherry MX Keyswitch Simple
  MX11 = Cherry MX Keyswitch Simple
  MX12 = Cherry MX Keyswitch Simple
  μUSB = USB Connectors [package=usb-microb]
  D1 = Diode [package=sma-diode-kit]
  D2 = Diode [package=sma-diode-kit]
  D3 = Diode [package=sma-diode-kit]
  D4 = Diode [package=sma-diode-kit]
  D5 = Diode [package=sma-diode-kit]
  D6 = Diode [package=sma-diode-kit]
  D7 = Diode [package=sma-diode-kit]
  D8 = Diode [package=sma-diode-kit]
  D9 = Diode [package=sma-diode-kit]
  D10 = Diode [package=sma-diode-kit]
  D11 = Diode [package=sma-diode-kit]
  D12 = Diode [package=sma-diode-kit]
  RE1 = Rotary Encoder [package=THT]
  RE2 = Rotary Encoder [package=THT]
  ESP32-S2 = ESP32-S2-DevKitM-1 [part_number=ESP32-S2-DevKitM-1]
  J1 = female pin header, 26 pins [form="♀ (female)"]

nets (from the pcb view):
  N1: MX1.pin_1, MX2.pin_1, MX3.pin_1, ESP32-S2.4
  N2: MX1.pin_2, D1.A
  N3: MX2.pin_2, D2.A
  N4: MX3.pin_2, D3.A
  N5: MX4.pin_1, MX5.pin_1, MX6.pin_1, ESP32-S2.3
  N6: MX4.pin_2, D4.A
  N7: MX5.pin_2, D5.A
  N8: MX6.pin_2, D6.A
  N9: MX7.pin_1, MX8.pin_1, MX9.pin_1, ESP32-S2.2
  N10: MX7.pin_2, D7.A
  N11: MX8.pin_2, D8.A
  N12: MX9.pin_2, D9.A
  N13: MX10.pin_1, MX11.pin_1, MX12.pin_1, ESP32-S2.1
  N14: MX10.pin_2, D10.A
  N15: MX11.pin_2, D11.A
  N16: MX12.pin_2, D12.A
  N17: μUSB.D+, ESP32-S2.20
  N18: μUSB.D-, ESP32-S2.19
  N19: μUSB.GND, RE1.EncoderPinC, RE1.SwitchrPinD, RE2.EncoderPinC, RE2.SwitchPinE, ESP32-S2.42, ESP32-S2.G-21, ESP32-S2.G-42, J1.pin12, J1.pin25
  N20: μUSB.VBUS, ESP32-S2.5V
  N21: D1.C, D4.C, D7.C, D10.C, ESP32-S2.10
  N22: D2.C, D5.C, D8.C, D11.C, ESP32-S2.11
  N23: D3.C, D6.C, D9.C, D12.C, ESP32-S2.12
  N24: RE1.EncoderPinA, ESP32-S2.37
  N25: RE1.EncoderPinB, ESP32-S2.38
  N26: RE2.EncoderPinA, ESP32-S2.39
  N27: RE2.EncoderPinB, ESP32-S2.40
  N28: RE2.SwitchrPinD, ESP32-S2.41
  N29: ESP32-S2.18, J1.pin11
  N30: ESP32-S2.21, J1.pin10
  N31: ESP32-S2.26, J1.pin9
  N32: ESP32-S2.33, J1.pin8
  N33: ESP32-S2.34, J1.pin7
  N34: ESP32-S2.35, J1.pin6
  N35: ESP32-S2.36, J1.pin5
  N36: ESP32-S2.TX, J1.pin4
  N37: ESP32-S2.RX, J1.pin3
  N38: ESP32-S2.45, J1.pin2
  N39: ESP32-S2.46, J1.pin1
  N40: ESP32-S2.RST, J1.pin24
  N41: ESP32-S2.3V3, J1.pin26
  N42: ESP32-S2.0, J1.pin23
  N43: ESP32-S2.5, J1.pin22
  N44: ESP32-S2.6, J1.pin21
  N45: ESP32-S2.7, J1.pin20
  N46: ESP32-S2.8, J1.pin19
  N47: ESP32-S2.9, J1.pin18
  N48: ESP32-S2.13, J1.pin17
  N49: ESP32-S2.14, J1.pin16
  N50: ESP32-S2.15, J1.pin15
  N51: ESP32-S2.16, J1.pin14
  N52: ESP32-S2.17, J1.pin13

notes:
  Pooky'
  Rev 2
  16/05/2021
  CyberDeck Keypad, A 12-key programmable keypad made for a CyberDeck project using an ESP32-S2 for Wi-Fi capabilities., 2
  Test 2
  gnd
  5V
  Raw 1
  Raw 2
  Raw 3
  Col 1
  Col 2
  Col 3
  Col 4
  D-
  D+
  3V3
  Gnd
  Rst
  0
  5
  6
  7
  8
  9
  13
  14
  15
  16
  17
  LED
  18
  21
  26
  33
  34
  35
  36
  37
  38
  39
  40
  41
  42
  TX
  RX
  JLCJLCJLCJLC

custom parts:
  Cherry MX Keyswitch Simple: Cherry MX Keyswitch button for keyboards
  Rotary Encoder: Rotary Encoder from ALPSec11e with switch. This version has an alternate (which has been used in boards) pcb footprint from @opera_night in the forums. It is probably the best one to start from to see if you part matches.
  ESP32-S2-DevKitM-1: The DOIT Esp32 DevKit v1 is one of the development board created by DOIT to evaluate the ESP-WROOM-32 module. It is based on the ESP32 microcontroller that boasts Wifi, Bluetooth, Ethernet and Low Power support all in a single chip. (vanepp) Feb 2021: converted to ESP32-S2-DevKitM-1. This module is 42pins long (2x21) and 11 pins width.
