# Fritzing sketch kbd_projekt_no_encoder (saved by Fritzing 0.9.6b)
circuit board: 10.87cm x 8.35169cm

parts:
  ESP32-S2 = ESP32-S2-DevKitM-1 [part_number=ESP32-S2-DevKitM-1]
  MX1 = Cherry MX Keyswitch Simple
  MX2 = Cherry MX Keyswitch Simple
  MX3 = Cherry MX Keyswitch Simple
  MX4 = Cherry MX Keyswitch Simple
  MX5 = Cherry MX Keyswitch Simple
  MX6 = Cherry MX Keyswitch Simple
  MX7 = Cherry MX Keyswitch Simple
  MX8 = Cherry MX Keyswitch Simple
  MX9 = Cherry MX Keyswitch Simple
  MX10 = Cherry MX Keyswitch Simple
  MX11 = Cherry MX Keyswitch Simple
  MX12 = Cherry MX Keyswitch Simple
  μUSB = USB Connectors [package=usb-microb]
  D1 = Diode [package=sma-diode-kit]
  D2 = Diode [package=sma-diode-kit]
  D3 = Diode [package=sma-diode-kit]
  D4 = Diode [package=sma-diode-kit]
  D5 = Diode [package=sma-diode-kit]
  D6 = Diode [package=sma-diode-kit]
  D7 = Diode [package=sma-diode-kit]
  D8 = Diode [package=sma-diode-kit]
  D9 = Diode [package=sma-diode-kit]
  D10 = Diode [package=sma-diode-kit]
  D11 = Diode [package=sma-diode-kit]
  D12 = Diode [package=sma-diode-kit]
  J1 = female pin header, 32 pins [form="♀ (female)"]

nets:
  18: ESP32-S2.18, J1.pin17
  Data -: ESP32-S2.19, μUSB.D-
  Data +: ESP32-S2.20, μUSB.D+
  21: ESP32-S2.21, J1.pin16
  26: ESP32-S2.26, J1.pin15
  33: ESP32-S2.33, J1.pin14
  34: ESP32-S2.34, J1.pin13
  35: ESP32-S2.35, J1.pin12
  36: ESP32-S2.36, J1.pin11
  37: ESP32-S2.37, J1.pin10
  38: ESP32-S2.38, J1.pin9
  39: ESP32-S2.39, J1.pin8
  40: ESP32-S2.40, J1.pin7
  41: ESP32-S2.41, J1.pin6
  42: ESP32-S2.42, J1.pin5
  TX: ESP32-S2.TX, J1.pin4
  RX: ESP32-S2.RX, J1.pin3
  45: ESP32-S2.45, J1.pin2
  46: ESP32-S2.46, J1.pin1
  Rst: ESP32-S2.RST, J1.pin30
  Gnd/Gnd1: ESP32-S2.G-21, ESP32-S2.G-42, μUSB.GND, J1.pin18, J1.pin31
  3V3: ESP32-S2.3V3, J1.pin32
  0: ESP32-S2.0, J1.pin29
  Span 1: ESP32-S2.1, MX10.pin_1, MX11.pin_1, MX12.pin_1
  Span 2: ESP32-S2.2, MX7.pin_1, MX8.pin_1, MX9.pin_1
  Span 3: ESP32-S2.3, MX4.pin_1, MX5.pin_1, MX6.pin_1
  Span 4: ESP32-S2.4, MX1.pin_1, MX2.pin_1, MX3.pin_1
  5: ESP32-S2.5, J1.pin28
  6: ESP32-S2.6, J1.pin27
  7: ESP32-S2.7, J1.pin26
  8: ESP32-S2.8, J1.pin25
  9: ESP32-S2.9, J1.pin24
  Row 1: ESP32-S2.10, D1.C, D4.C, D7.C, D10.C
  Row 2: ESP32-S2.11, D2.C, D5.C, D8.C, D11.C
  Row 3: ESP32-S2.12, D3.C, D6.C, D9.C, D12.C
  13: ESP32-S2.13, J1.pin23
  14: ESP32-S2.14, J1.pin22
  15: ESP32-S2.15, J1.pin21
  16: ESP32-S2.16, J1.pin20
  17: ESP32-S2.17, J1.pin19
  5V: ESP32-S2.5V, μUSB.VBUS
  N1: MX1.pin_2, D1.A
  N2: MX2.pin_2, D2.A
  N3: MX3.pin_2, D3.A
  N4: MX4.pin_2, D4.A
  N5: MX5.pin_2, D5.A
  N6: MX6.pin_2, D6.A
  N7: MX7.pin_2, D7.A
  N8: MX8.pin_2, D8.A
  N9: MX9.pin_2, D9.A
  N10: MX10.pin_2, D10.A
  N11: MX11.pin_2, D11.A
  N12: MX12.pin_2, D12.A

notes:
  Pooky'
  Rev 2
  15/05/2021
  CyberDeck Keypad, A 12-key programmable keypad made for a CyberDeck project using an ESP32-S2 for Wi-Fi capabilities., 2
  Test 2
  gnd
  5V
  Raw 1
  Raw 2
  Raw 3
  Col 1
  Col 2
  Col 3
  Col 4
  D-
  D+
  RX
  TX
  42
  41
  36
  35
  34
  33
  26
  21
  18
  Gnd
  17
  16
  15
  14
  13
  9
  8
  7
  6
  5
  0
  Rst
  3V3
  40
  39
  38
  37

custom parts:
  ESP32-S2-DevKitM-1: The DOIT Esp32 DevKit v1 is one of the development board created by DOIT to evaluate the ESP-WROOM-32 module. It is based on the ESP32 microcontroller that boasts Wifi, Bluetooth, Ethernet and Low Power support all in a single chip. (vanepp) Feb 2021: converted to ESP32-S2-DevKitM-1. This module is 42pins long (2x21) and 11 pins width.
  Cherry MX Keyswitch Simple: Cherry MX Keyswitch button for keyboards
